# Fritzing sketch 33-HandScanner (saved by Fritzing 1.0.6)
breadboards: 1

parts:
  Ledstrip = SMD RGB LED (WS2812) [package=5050]
  Nano = Arduino Nano (Rev3.0)
  knop = Square Pushbutton
  R9 = Resistor [tolerance=±5% resistance=470 package="0603 [SMD]"]
  1000uF_25V = Capacitor Polarized [package=panasonic_g]
  R13 = Resistor [tolerance=±5% resistance=470k package="0603 [SMD]"]

nets:
  N1: Ledstrip.DIn, R9.Pin_1
  12V: Ledstrip.VCC, Nano.5V
  GND: Ledstrip.VSS, knop.leg1, 1000uF_25V.-
  N2: Nano.D3, R13.Pin_0
  N3: Nano.D4, R13.Pin_1
  N4: Nano.A0, R9.Pin_0

notes:
  Spiegel
  TouchPlaat
