# Fritzing sketch 47b-KikkerkokenOutput (saved by Fritzing 1.0.6)
circuit board: 12.5227cm x 9.27753cm
breadboards: 1

parts:
  Strip_1 = SMD RGB LED (WS2812) [package=5050]
  Ledstrip_2 = SMD RGB LED (WS2812) [package=5050]
  5 = Square Pushbutton
  4 = Square Pushbutton
  3 = Square Pushbutton
  2 = Square Pushbutton
  1 = Square Pushbutton
  1000uF_25V = Capacitor Polarized [package=panasonic_g]
  1000uF_25V_2 = Capacitor Polarized [package=panasonic_g]
  R5 = Resistor [tolerance=±5% resistance=470 power=0.25W package=THT]
  R4 = Resistor [tolerance=±5% resistance=470 power=0.25W package=THT]
  Nano = Arduino Pro Mini v13
  BUBBELS_EN_STOOM = SMD RGB LED (WS2812) [package=5050]

nets:
  N1: Strip_1.DIn, R4.Pin_1
  VCC: Strip_1.VCC, Ledstrip_2.VCC, 1000uF_25V.+, 1000uF_25V_2.+
  N2: Strip_1.VSS, 5.leg1, 4.leg1, 3.leg1, 2.leg1, 1.leg1, 1000uF_25V_2.-
  N3: Ledstrip_2.DIn, R5.Pin_1
  N4: Ledstrip_2.VSS, 1000uF_25V.-
  N5: 5.leg0, Nano.D6_PWM
  N6: 4.leg0, Nano.D5_PWM
  N7: 3.leg0, Nano.D4
  N8: 2.leg0, Nano.D3_PWM
  N9: 1.leg0, Nano.D2
  N10: R5.Pin_0, Nano.A1
  N11: R4.Pin_0, Nano.A0
  5V: Nano.VCC
  N12: Nano.A2, BUBBELS_EN_STOOM.DIn
